# Fritzing sketch panzer (saved by Fritzing 0.9.3b)

parts:
  WF1 = chipKIT WF32 [package=WF32]
  S1 = H-Bridge with L298N
  Part1 = Bluetooth HC-05 Macho
  U2 = LIPO-1000mAh [package=lipo-1000]
  U3 = LIPO-1000mAh [package=lipo-1000]
  U4 = LIPO-1000mAh [package=lipo-1000]
  J1 = Basic Servo  # not connected
  J2 = Basic Servo

nets:
  3V3: WF1.3V3, Part1.VCC
  N1: WF1.5V0, J2.vcc
  N2: WF1.GND#5, Part1.GND
  GND: WF1.GND#6, S1.GND, U4.-, J2.gnd
  VIN: WF1.VIN, S1.5V
  N3: WF1.D2, S1.ENA
  N4: WF1.D3, S1.ENB
  N5: WF1.D4, S1.IN1
  N6: WF1.D13, J2.pulse
  N7: WF1.D26, Part1.TXD
  N8: WF1.D27, Part1.RXD
  N9: WF1.D28, S1.IN4
  N10: WF1.D29, S1.IN3
  N11: WF1.D30, S1.IN2
  N12: S1.12V, U2.+
  N13: U2.-, U3.+
  N14: U3.-, U4.+

custom parts:
  H-Bridge with L298N: h-bridge
